# Fritzing sketch Diagrama de conexion (saved by Fritzing 0.9.3b)

parts:
  Part1 = 16-Channel 12-bit PCA9685 PWM/Servo Driver
  Part2 = Arduino Uno (Rev3)
  JACK1 = 2.1mm Barrel Jack with Terminal Block
  J1 = Basic Servo

nets:
  N1: Part1.PWRIN, JACK1.POS
  GND: Part1.GND, Part2.GND, JACK1.NEG, J1.gnd
  N2: Part1.0, J1.pulse
  N3: Part1.V+, J1.vcc
  VCC: Part1.VCC, Part2.5V
  N4: Part1.SDA, Part2.A4/SDA
  N5: Part1.SCL, Part2.A5/SCL

custom parts:
  16-Channel 12-bit PCA9685 PWM/Servo Driver: The Adafruit 16-Channel 12-bit PWM/Servo Driver will drive up to 16 servos over I2C with only 2 pins. The on-board PCA9685 PWM controller will drive all 16 channels simultaneously with no additional processing overhead. What's more, you can chain up to 62 of them to control up to 992 servos - all with the same 2 pins
